# Fritzing sketch The Tricorder Project - Mark I (saved by Fritzing 0.9.0b)
circuit board: 18.1712cm x 10.2628cm

parts:
  Fio = Arduino Fio (Funnel I/O)
  SHT15 = Humidity Temperature Sensor SHT15
  Nokia_5110_LCD_Module1 = Nokia5110LCDModule
  TSL1 = TSL2561 Breakout Board [package="DIP (Dual Inline) [THT]"]
  LED1 = LED - 5mm [color="Red (633nm)" package="5 mm [THT]"]
  R1 = Resistor [tolerance=±5% resistance=220 package=THT]
  S1 = Pushbutton [package="[THT]"]
  R2 = Resistor [tolerance=±5% resistance=10k package=THT]
  R3 = Resistor [tolerance=±5% resistance=10k package="0805 [SMD]"]

nets:
  VCC: Fio.VCC, Nokia_5110_LCD_Module1.Vcc, S1.Pin_3, S1.Pin_4
  GND: Fio.GND, SHT15.GND, Nokia_5110_LCD_Module1.Grnd, TSL1.GND, LED1.cathode, R2.Pin_0
  N1: Fio.D2, S1.Pin_1, S1.Pin_2, R2.Pin_1
  N2: Fio.D3_PWM, SHT15.SDA, R3.Pin_1
  N3: Fio.D4, SHT15.SCL
  N4: Fio.D5_PWM, R1.Pin_1
  N5: Fio.D6_PWM, Nokia_5110_LCD_Module1.LED
  N6: Fio.D7, TSL1.VDD
  N7: Fio.D8, Nokia_5110_LCD_Module1.SCE
  N8: Fio.D9_PWM, Nokia_5110_LCD_Module1.RST
  N9: Fio.D10_PWM/SS, Nokia_5110_LCD_Module1.D/C
  N10: Fio.D11_PWM/MOSI, Nokia_5110_LCD_Module1.6_DN_(MOSI)
  N11: Fio.D12/MISO, SHT15.VCC, R3.Pin_0
  N12: Fio.D13/SCK, Nokia_5110_LCD_Module1.SCLK
  N13: Fio.A4/SDA, TSL1.SDA
  N14: Fio.A5/SCL, TSL1.SCL
  N15: LED1.anode, R1.Pin_0

custom parts:
  : Nokia 5110 LCD with 8 pin. It's a 45mm*45mm module part. Description: The Nokia 5110 is a basic graphic LCD screen for lots of applications. It was originally intended for as a cell phone screen. This one is mounted on an easy to solder PCB. It uses the PCD8544 controller. The PCD8544 is a low power CMOS LCD controller/driver, designed to drive a graphic display of 48 rows and 84 columns. All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
  TSL2561 Breakout Board: The TSL2561 Luminosity Sensor Breakout is a sophisticated light sensor which has a flat response across most of the visible spectrum. Unlike simpler sensors, the TSL2561 measures both infrared and visible light to better approximate the response of the human eye. And because the TSL2561 is an integrating sensor (it soaks up light for a predetermined amount of time), it is capable of measuring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
