# Fritzing sketch The Tricorder Project (saved by Fritzing 0.9.1b)
circuit board: 8.46667cm x 5.64444cm

parts:
  Adafruit_SD_logging_shield_with_RTC = Memoire 1.0 - SD card log shield
  Light_Sensor = IC, DIP package, 6 pins [chip_label=TSL2591]
  Soil_Sensor = SHT1x Humdity Sensor [package=sht1x]
  GUVA-S12SD = S1133 Si Photodiode [part_number="UV Sensor" package="8mm Ceramic [THT]"]
  U1 = OPA344 [package=sot23-5]
  C1 = Ceramic Capacitor [capacitance=100nF package="100 mil [THT, multilayer]"]
  C2 = Ceramic Capacitor [capacitance=100nF package="100 mil [THT, multilayer]"]
  R2 = Resistor [tolerance=±5% resistance=3.3k package=THT]
  R3 = Resistor [tolerance=±5% resistance=1M package=THT]
  Power = DC Power [voltage=9 frequency=60]
  R4 = Resistor [tolerance=±5% resistance=10k package="0805 [SMD]"]
  R5 = Resistor [tolerance=±5% resistance=10k package="0805 [SMD]"]
  R6 = Resistor [tolerance=±5% resistance=10k package="0805 [SMD]"]
  R7 = Resistor [tolerance=±5% resistance=10k package="0805 [SMD]"]
  Q1 = Basic FET P-Channel [part_number=BSS138 package="D2Pak [SMD]"]
  Q2 = Basic FET P-Channel [part_number=BSS138 package="D2Pak [SMD]"]
  C3 = Ceramic Capacitor [capacitance=10µF package="100 mil [THT, multilayer]"]
  MIC5219-3_3V = V_REG MIC5219 [package=sot23-5]
  C4 = Ceramic Capacitor [capacitance=10µF package="100 mil [THT, multilayer]"]
  ATMEGA_328 = Arduino Uno (Rev3) - ICSP
  Air_Sensor = IC, DIP package, 6 pins [chip_label=HTU21DF]

nets:
  D8: Adafruit_SD_logging_shield_with_RTC.DIG_8, ATMEGA_328.D8
  D9: Adafruit_SD_logging_shield_with_RTC.DIG_9, ATMEGA_328.D9_PWM
  D10/SS: Adafruit_SD_logging_shield_with_RTC.DIG_10
  D11/MOSI: Adafruit_SD_logging_shield_with_RTC.DIG_11
  D12/MISO: Adafruit_SD_logging_shield_with_RTC.DIG_12
  D13/SCK: Adafruit_SD_logging_shield_with_RTC.DIG_13, ATMEGA_328.D13/SCK
  GND: Adafruit_SD_logging_shield_with_RTC.GND, Light_Sensor.pin3, Soil_Sensor.GND, GUVA-S12SD.cathode, U1.V-, U1.+IN, C2.0, Power.V-, C3.0, MIC5219-3_3V.GND, C4.0, ATMEGA_328.GND, Air_Sensor.pin2
  AREF: Adafruit_SD_logging_shield_with_RTC.AREF, ATMEGA_328.AREF
  D0: Adafruit_SD_logging_shield_with_RTC.DIG_0, ATMEGA_328.D0/RX
  D1: Adafruit_SD_logging_shield_with_RTC.DIG_1, ATMEGA_328.D1/TX
  D3: Adafruit_SD_logging_shield_with_RTC.DIG_3, ATMEGA_328.D3_PWM
  D4: Adafruit_SD_logging_shield_with_RTC.DIG_4, ATMEGA_328.D4
  D5: Adafruit_SD_logging_shield_with_RTC.DIG_5, ATMEGA_328.D5_PWM
  D6: Adafruit_SD_logging_shield_with_RTC.DIG_6, ATMEGA_328.D6_PWM
  A0: Adafruit_SD_logging_shield_with_RTC.A_IN_0, ATMEGA_328.A0
  SCL: Adafruit_SD_logging_shield_with_RTC.A_IN_5, Air_Sensor.pin4
  D2: Adafruit_SD_logging_shield_with_RTC.DIG_2, ATMEGA_328.D2
  D7: Adafruit_SD_logging_shield_with_RTC.DIG_7, ATMEGA_328.D7
  A1: Adafruit_SD_logging_shield_with_RTC.A_IN_1, U1.OUT, R2.Pin_0, ATMEGA_328.A1
  A2: Adafruit_SD_logging_shield_with_RTC.A_IN_2, Soil_Sensor.SCK, ATMEGA_328.A2
  A3: Adafruit_SD_logging_shield_with_RTC.A_IN_3, Soil_Sensor.DATA, ATMEGA_328.A3
  SDA: Adafruit_SD_logging_shield_with_RTC.A_IN_4, Air_Sensor.pin3
  RESET: Adafruit_SD_logging_shield_with_RTC.RESET, ATMEGA_328.RESET
  3.3V: Adafruit_SD_logging_shield_with_RTC.3V3, Light_Sensor.pin5, R5.Pin_0, R7.Pin_1, Q1.Gate, Q2.Gate, MIC5219-3_3V.OUT, C4.1, ATMEGA_328.3V3
  Vin: Adafruit_SD_logging_shield_with_RTC.VIN, Power.V+, ATMEGA_328.VIN
  SCL_3.3V: Light_Sensor.pin1, R7.Pin_0, Q1.source
  SDA_3.3V: Light_Sensor.pin6, R5.Pin_1, Q2.source
  5V: Soil_Sensor.VDD, U1.V+, C2.1, R4.Pin_0, R6.Pin_1, C3.1, MIC5219-3_3V.IN, MIC5219-3_3V.EN, ATMEGA_328.5V, Air_Sensor.pin5
  N1: GUVA-S12SD.anode, U1.-IN, C1.0, R3.Pin_0
  N2: C1.1, R2.Pin_1, R3.Pin_1
  SDA_5.0V: R4.Pin_1, Q2.drain, ATMEGA_328.A4/SDA
  SCL_5.0V: R6.Pin_0, Q1.drain, ATMEGA_328.A5/SCL
